# Fritzing sketch actuadorAnalogico (saved by Fritzing 0.9.3b)
breadboards: 1

parts:
  Part1 = Arduino Uno (Rev3)
  Part2 = KY-008 Laser Transmitter Module [package="Breakout board"]

nets:
  N1: Part1.D3_PWM, Part2.S
  N2: Part1.GND, Part2.-

custom parts:
  KY-008 Laser Transmitter Module: Laser Transmitter module KY-008 for Arduino, emits a dot shaped red laser beam.
