# Fritzing sketch IRmando (saved by Fritzing 0.9.3b)
breadboards: 1

parts:
  Part1 = Arduino Uno (Rev3)
  Part2 = KY-022 Infrared Receiver Module [package="Breakout board"]

nets:
  N1: Part1.D2, Part2.S
  5V: Part1.5V, Part2.Vin
  N2: Part1.GND, Part2.-

custom parts:
  KY-022 Infrared Receiver Module: Arduino IR receiver module KY-022, reacts to 38kHz infrared light.
