# Fritzing sketch rtc1302 (saved by Fritzing 0.9.3b)
breadboards: 1

parts:
  PCB2 = RTC_DS1302_module
  Part1 = Arduino Uno (Rev3)

nets:
  VCC: PCB2.VCC, Part1.5V
  GND: PCB2.GND, Part1.GND
  N1: PCB2.RST, Part1.D8
  N2: PCB2.DAT, Part1.D7
  N3: PCB2.CLK, Part1.D6_PWM

custom parts:
  RTC_DS1302_module: Arduino module DS1302 SPI Real Time Clock
