# Fritzing sketch dfplayer (saved by Fritzing 0.9.3b)
breadboards: 1

parts:
  DFRobot_DFPlayer_Mini1 = DFRobot DFPlayer Mini [part_number=DFR0299]
  Part1 = Arduino Uno (Rev3)
  SP1 = SPEAKER [package=pcb_mount_speaker]
  R1 = Resistor [tolerance=±5% resistance=1k package=THT]

nets:
  VCC: DFRobot_DFPlayer_Mini1.VCC, Part1.5V
  N1: DFRobot_DFPlayer_Mini1.RX, R1.Pin_1
  N2: DFRobot_DFPlayer_Mini1.TX, Part1.D10_PWM/SS
  N3: DFRobot_DFPlayer_Mini1.SPK_1, SP1.-
  N4: DFRobot_DFPlayer_Mini1.GND-1, DFRobot_DFPlayer_Mini1.GND-2, Part1.GND
  N5: DFRobot_DFPlayer_Mini1.SPK_2, SP1.+
  N6: Part1.D11_PWM/MOSI, R1.Pin_0
