# Fritzing sketch motorDC (saved by Fritzing 0.9.3b)
breadboards: 1

parts:
  S1 = H-Bridge with L298N
  Part1 = Arduino Uno (Rev3)
  Power_plug1 = Power plug
  M1 = DC Motor
  M2 = DC Motor

nets:
  12V: S1.12V, Power_plug1.VCC
  GND: S1.GND, Part1.GND, Power_plug1.GND
  N1: S1.ENA, Part1.D10_PWM/SS
  N2: S1.IN1, Part1.D9_PWM
  N3: S1.IN2, Part1.D8
  N4: S1.IN3, Part1.D7
  N5: S1.IN4, Part1.D6_PWM
  N6: S1.ENB, Part1.D5_PWM
  N7: S1.M1-01, M2.pin_2
  N8: S1.M1-02, M2.pin_1
  N9: S1.M2-01, M1.pin_2
  N10: S1.M2-02, M1.pin_1

custom parts:
  H-Bridge with L298N: h-bridge
