# Fritzing sketch motorPasoPaso (saved by Fritzing 0.9.3b)
breadboards: 1

parts:
  Part1 = Arduino Uno (Rev3)
  MOTOR1 = 28BYJ-48 Stepper Motor
  BREAKOUT1 = ULN2003A breakout board
  VCC1 = Battery

nets:
  N1: Part1.D2, BREAKOUT1.In_1
  N2: Part1.D3_PWM, BREAKOUT1.In_2
  N3: Part1.D4, BREAKOUT1.In_3
  N4: Part1.D5_PWM, BREAKOUT1.In_4
  N5: MOTOR1.RED, BREAKOUT1.RED_wire
  N6: MOTOR1.ORANGE, BREAKOUT1.ORANGE_wire
  N7: MOTOR1.YELLOW, BREAKOUT1.YELLOW_wire
  N8: MOTOR1.PINK, BREAKOUT1.PINK_wire
  N9: MOTOR1.BLUE, BREAKOUT1.BLUE_wire
  N10: BREAKOUT1.0V, VCC1.-
  N11: BREAKOUT1.+5V, VCC1.+

custom parts:
  ULN2003A breakout board: ULN2003A 7-way Darlington Transistor Driver on breakoutboard
