# Fritzing sketch potenciometro (saved by Fritzing 0.9.3b)
breadboards: 1

parts:
  Part1 = Arduino Uno (Rev3)
  R1 = Resistor [tolerance=±5% resistance=220 package=THT]
  LED1 = smd LED [color="Red (633nm)" package="0603 [SMD]"]
  R2 = Trimmer Potentiometer [maximum_resistance=10kΩ package=THT]

nets:
  N1: Part1.A0, R2.wiper
  N2: Part1.D3_PWM, LED1.anode
  N3: Part1.5V, R2.leg1
  N4: Part1.GND, R1.Pin_0, R2.leg2
  N5: R1.Pin_1, LED1.cathode
