# Fritzing sketch sensorDigital (saved by Fritzing 0.9.3b)
breadboards: 1

parts:
  Part1 = Arduino Uno (Rev3)
  Part2 = KY-021 Mini Magnetic Reed Switch Module [package="Breakout board"]

nets:
  N1: Part1.D2, Part2.S
  5V: Part1.5V, Part2.Vin
  N2: Part1.GND, Part2.-

custom parts:
  KY-021 Mini Magnetic Reed Switch Module: KY-021 magnetic reed switch module. A reed switch is a magnetic sensor that is normally open and gets closed when exposed to a magnetic field.
