# Fritzing sketch ultrasonido (saved by Fritzing 0.9.3b)
breadboards: 1

parts:
  Part1 = Arduino Uno (Rev3)
  Part2 = HC-SR04

nets:
  N1: Part1.D2, Part2.Trig
  N2: Part1.D3_PWM, Part2.Echo
  5V: Part1.5V, Part2.Vcc
  GND: Part1.GND, Part2.Gnd

custom parts:
  HC-SR04: HC-SR04 ultrasonic distance sensor
