# Fritzing sketch MusicStaveButtonLCD (saved by Fritzing 0.9.3b)
breadboards: 1

parts:
  Part1 = Arduino Uno (Rev3)
  SP1 = SPEAKER [package=pcb_mount_speaker]
  SP2 = SPEAKER [package=pcb_mount_speaker]
  R1 = Resistor [tolerance=±5% resistance=220 package=THT]
  R2 = Resistor [tolerance=±5% resistance=220 package=THT]
  S1 = Pushbutton [package="[THT]"]
  S2 = Pushbutton [package="[THT]"]
  S3 = Pushbutton [package="[THT]"]
  S4 = Pushbutton [package="[THT]"]
  LCD1 = LCD screen
  LCM1602_IIC1 = LCM1602 IIC [part_number="LCM1602 IIC" chip_label="LCM1602 IIC" package="DIP (Dual Inline) [THT]"]

nets:
  N1: Part1.D8, R2.Pin_0
  N2: Part1.D9_PWM, R1.Pin_0
  N3: Part1.A4/SDA, LCM1602_IIC1.SDA
  N4: Part1.A5/SCL, LCM1602_IIC1.SCL
  GND: Part1.D2, Part1.D3_PWM, Part1.D4, Part1.GND, SP1.+, SP2.+, S1.Pin_3, S1.Pin_4, S2.Pin_3, S2.Pin_4, S3.Pin_3, S3.Pin_4, S4.Pin_3, S4.Pin_4, LCM1602_IIC1.GND
  5V: Part1.5V, LCM1602_IIC1.VCC
  N5: SP1.-, R1.Pin_1
  N6: SP2.-, R2.Pin_1
  VSS: LCD1.VSS, LCM1602_IIC1.VSS
  VDD: LCD1.VDD, LCM1602_IIC1.VDD
  N7: LCD1.V0, LCM1602_IIC1.V0
  N8: LCD1.RS, LCM1602_IIC1.RS
  N9: LCD1.R/W, LCM1602_IIC1.RW
  N10: LCD1.E, LCM1602_IIC1.E
  N11: LCD1.DB0, LCM1602_IIC1.D0
  N12: LCD1.DB1, LCM1602_IIC1.D1
  N13: LCD1.DB2, LCM1602_IIC1.D2
  N14: LCD1.DB3, LCM1602_IIC1.D3
  N15: LCD1.DB4, LCM1602_IIC1.D4
  N16: LCD1.DB5, LCM1602_IIC1.D5
  N17: LCD1.DB6, LCM1602_IIC1.D6
  N18: LCD1.DB7, LCM1602_IIC1.D7
  N19: LCD1.LED+, LCM1602_IIC1.A
  N20: LCD1.LED-, LCM1602_IIC1.K
  N21: LCM1602_IIC1.LED_A, LCM1602_IIC1.LED_B

notes:
  PLAY
  PAUSE
  STOP
  LOOP

custom parts:
  LCM1602 IIC: I2C-Module to use a 1602 or 2004 LCD on with the wire.h libory Serial LCD Modul
