# Fritzing sketch MusicStave (saved by Fritzing 0.9.3b)

parts:
  Part1 = Arduino Uno (Rev3)
  SP1 = SPEAKER [package=pcb_mount_speaker]
  SP2 = SPEAKER [package=pcb_mount_speaker]
  R1 = Resistor [tolerance=±5% resistance=220 package=THT]
  R2 = Resistor [tolerance=±5% resistance=220 package=THT]

nets:
  N1: Part1.D8, R2.Pin_0
  N2: Part1.D9_PWM, R1.Pin_0
  N3: Part1.GND, SP1.+, SP2.+
  N4: SP1.-, R1.Pin_1
  N5: SP2.-, R2.Pin_1
