# Fritzing sketch FritzingBrazo (saved by Fritzing 0.9.3b)
breadboards: 1

parts:
  Componente1 = Arduino Uno (Rev3) - ICSP
  Matrix_keypad1 = KEYPAD 4x4
  Componente2 = Thumb Joystick
  Componente3 = Thumb Joystick
  J1 = Basic Servo
  J2 = Basic Servo
  J3 = Basic Servo
  J4 = Basic Servo
  LCD1 = LCD screen
  LCM1602_IIC1 = LCM1602 IIC [part_number="LCM1602 IIC" chip_label="LCM1602 IIC" package="DIP (Dual Inline) [THT]"]
  VCC1 = Battery

nets:
  N1: Componente1.A0, Componente2.HORZ
  N2: Componente1.A1, Componente2.VERT
  N3: Componente1.A2, Componente3.HORZ
  N4: Componente1.A3, Componente3.VERT
  N5: Componente1.D8, J1.pulse
  N6: Componente1.D9_PWM, J2.pulse
  N7: Componente1.D10_PWM/SS, J3.pulse
  N8: Componente1.D11_PWM/MOSI, J4.pulse
  N9: Componente1.A4/SDA, LCM1602_IIC1.SDA
  N10: Componente1.A5/SCL, LCM1602_IIC1.SCL
  N11: Componente1.D2, Matrix_keypad1.col1
  N12: Componente1.D3_PWM, Matrix_keypad1.col2
  N13: Componente1.D4, Matrix_keypad1.col3
  N14: Componente1.D5_PWM, Matrix_keypad1.col4
  N15: Componente1.D6_PWM, Matrix_keypad1.row1
  N16: Componente1.D7, Matrix_keypad1.row2
  VCC: Componente1.5V, Componente2.VCC, Componente3.VCC, LCM1602_IIC1.VCC
  GND: Componente1.GND, Componente2.GND, Componente3.GND, LCM1602_IIC1.GND
  GND_2: J1.gnd, J2.gnd, J3.gnd, J4.gnd, VCC1.-
  VCC_2: J1.vcc, J2.vcc, J3.vcc, J4.vcc, VCC1.+
  VSS: LCD1.VSS, LCM1602_IIC1.VSS
  VDD: LCD1.VDD, LCM1602_IIC1.VDD
  N17: LCD1.V0, LCM1602_IIC1.V0
  N18: LCD1.RS, LCM1602_IIC1.RS
  N19: LCD1.R/W, LCM1602_IIC1.RW
  N20: LCD1.E, LCM1602_IIC1.E
  N21: LCD1.DB0, LCM1602_IIC1.D0
  N22: LCD1.DB1, LCM1602_IIC1.D1
  N23: LCD1.DB2, LCM1602_IIC1.D2
  N24: LCD1.DB3, LCM1602_IIC1.D3
  N25: LCD1.DB4, LCM1602_IIC1.D4
  N26: LCD1.DB5, LCM1602_IIC1.D5
  N27: LCD1.DB6, LCM1602_IIC1.D6
  N28: LCD1.DB7, LCM1602_IIC1.D7
  N29: LCD1.LED+, LCM1602_IIC1.A
  N30: LCD1.LED-, LCM1602_IIC1.K
  N31: LCM1602_IIC1.LED_A, LCM1602_IIC1.LED_B

notes:
  Depende del keypad, las columnas empiezan por 1, o por 4, revisar bien el cableado, la columna 1 va a la entrada 2 del arduino
  Y la fila 1 va al 6 del arduino
  En este proyecto solo se utiliza una matriz de botones de 4x2

custom parts:
  KEYPAD 4x4: Matrix keypad 16 buttons, 4 rows x 4 columns
  LCM1602 IIC: I2C-Module to use a 1602 or 2004 LCD on with the wire.h libory Serial LCD Modul
