# Fritzing sketch esquema (saved by Fritzing 0.9.3b)
breadboards: 1

parts:
  2N2222 = NPN-Transistor [package="TO92 [THT]"]
  Arduino = Arduino Leonardo (Rev3b)
  Rele_1 = KY-019 5V Relay Module [package="Breakout board"]
  Rele_2 = KY-019 5V Relay Module [package="Breakout board"]
  Motor = DC Motor
  Bluetooth = Bluetooth HC-05 Macho
  VCC1 = Battery
  VCC2 = Battery

nets:
  GND: 2N2222.E, Arduino.GND, Rele_1.-, Rele_2.-, Bluetooth.GND, VCC1.-, VCC2.-
  N1: 2N2222.B, Arduino.D3_PWM/SCL, Arduino.SCL
  N2: 2N2222.C, Rele_1.Common
  N3: Arduino.D4/A6, Rele_1.S, Rele_2.S
  5V: Arduino.5V, Rele_1.+, Rele_2.+, Bluetooth.VCC
  N4: Arduino.VIN, VCC2.+
  N5: Arduino.D10_PWM/A10, Bluetooth.RXD
  N6: Arduino.D11_PWM, Bluetooth.TXD
  N7: Rele_1.NC, Rele_2.NO, Motor.pin_1
  N8: Rele_1.NO, Rele_2.NC, Motor.pin_2
  N9: Rele_2.Common, VCC1.+

custom parts:
  KY-019 5V Relay Module: KY-019 5V Relay module, used to control AC circuits.
